# Fritzing sketch Datalogging_SD_PCB_V1 (saved by Fritzing 0.9.3b)
circuit board: 7.36049cm x 3.86981cm
breadboards: 1

parts:
  ATmega = atmega328 [package=dip]
  AREF_A0-5 = male pin header, 7 pins [form="♂ (male)"]
  D4-D0 = male pin header, 5 pins [form="♂ (male)"]
  5v_in = male pin header, 1 pin [form="♂ (male)"]
  -_+ = male pin header, 1 pin [form="♂ (male)"]
  16MHz = Crystal [frequency="16 Mhz" package=THT]
  C3 = Capacitor [package=cap-pth-small2]
  C4 = Capacitor [package=cap-pth-small2]
  R1 = Resistor [tolerance=±5% resistance=220 package=THT]
  Reset = Momentary Switch [package=ksa_sealed_tac_switch]
  5v = male pin header, 4 pins [form="♂ (male)"]
  GND = male pin header, 4 pins [form="♂ (male)"]
  D5-13 = male pin header, 9 pins [form="♂ (male)"]
  RST = female pin header, 1 pin [form="♀ (female)"]
  L7805 = Voltage Regulator - 3.3V [package="TO220 [THT]"]
  -_+_2 = female pin header, 2 pins [form="♀ (female)"]
  C1 = Capacitor Polarized [package=cpol-radial-10uf-25v]
  C2 = Capacitor Polarized [package=cpol-radial-10uf-25v]
  SD = SD Card Slot [form="♀ (female)" package=THT]
  10K_R = male pin header, 1 pin [form="♂ (male)"]

nets:
  N1: ATmega.RESET, R1.Pin_0, Reset.1, RST.pin1
  N2: ATmega.D0_(RX), D4-D0.pin1
  N3: ATmega.D1_(TX), D4-D0.pin2
  N4: ATmega.D2, D4-D0.pin3
  N5: ATmega.D3_(PWM), D4-D0.pin4
  N6: ATmega.D4, D4-D0.pin5
  N7: ATmega.VCC, ATmega.AVCC, 5v_in.pin1, R1.Pin_1, 5v.pin1, 5v.pin2, 5v.pin3, 5v.pin4, L7805.output_voltage, C2.+, SD.3.3V_(4)
  GND: ATmega.GND, -_+.pin1, C3.2, C4.1, Reset.4, GND.pin1, GND.pin2, GND.pin3, GND.pin4, L7805.GND, -_+_2.pin1, C1.-, C2.-, SD.GND_(3)
  N8: ATmega.XLAT1, 16MHz.pin_0, C3.1
  N9: ATmega.XLAT2, 16MHz.pin_1, C4.2
  N10: ATmega.D5_(PWM), D5-13.pin9
  N11: ATmega.D6_(PWM), D5-13.pin8
  N12: ATmega.D7, D5-13.pin7
  N13: ATmega.D8, D5-13.pin6
  N14: ATmega.D9_(PWM), D5-13.pin5
  N15: ATmega.D10_(PWM), D5-13.pin4, SD.CS
  N16: ATmega.D11_(PWM), D5-13.pin3, SD.MOSI_(2)
  N17: ATmega.D12, D5-13.pin2, SD.SCK_(5)
  N18: ATmega.D13, D5-13.pin1, SD.MISO_(7)
  N19: ATmega.AREF, AREF_A0-5.pin7
  N20: ATmega.A0, AREF_A0-5.pin6
  N21: ATmega.A1, AREF_A0-5.pin5
  N22: ATmega.A2, AREF_A0-5.pin4
  N23: ATmega.A3, AREF_A0-5.pin3
  N24: ATmega.A4, AREF_A0-5.pin2
  N25: ATmega.A5, AREF_A0-5.pin1
  N26: L7805.input_voltage, -_+_2.pin2, C1.+
  N27: SD.GND_(6), 10K_R.pin1

notes:
  7.5-25v
  In order to use this board for SD data logging, SD pin must be set as:
  #define CS 10
  #define SCK 12
  #define MOSI 11
  #define MISO 13

custom parts:
  SD Card Slot: Generic female header
